// Logisim project alu.circ as structural Verilog: 3 circuits, main circuit alu
module alu (
  input  [31:0] A,
  input  [31:0] B,
  input  [3:0] ALUSel,
  output [31:0] Result
);

  wire comparator_1_lt;
  wire [6:0] bitadder_1_out;
  wire [31:0] adder_1_out, and_1_out, bit_extender_2_out, divider_2_out, mulh_1_out_3, multiplier_1_out,
       multiplier_2_cout, or_1_out, remu, sll0, slt0, sra0, srl0, subtractor_1_out, xor_1_out;

  Divider #(.width(32)) divider_1 (.a(A), .b(B), .rem(remu));  // open: out, upper
  Comparator #(.width(32)) comparator_1 (.a(A), .b(B), .lt(comparator_1_lt));  // open: gt, eq
  Shifter #(.width(32), .shift("lr")) shifter_1 (.in(A), .\dist (B[4:0]), .out(srl0));
  Shifter #(.width(32), .shift("ar")) shifter_2 (.in(A), .\dist (B[4:0]), .out(sra0));
  Shifter #(.width(32)) shifter_3 (.in(A), .\dist (B[4:0]), .out(sll0));
  assign slt0 = {{31{1'b0}}, comparator_1_lt};  // Bit_Extender bit_extender_1
  assign and_1_out = A & B;  // AND_Gate and_1, 32 bits wide
  assign or_1_out = A | B;  // OR_Gate or_1, 32 bits wide
  assign xor_1_out = A ^ B;  // XOR_Gate xor_1, 32 bits wide
  Adder #(.width(32)) adder_1 (.a(A), .b(B), .out(adder_1_out));  // open: cin, cout
  Subtractor #(.width(32)) subtractor_1 (.a(A), .b(B), .out(subtractor_1_out));  // open: bin, bout
  Multiplier #(.width(32)) multiplier_1 (.a(A), .b(B), .out(multiplier_1_out));  // open: cin, cout
  Multiplier #(.width(32)) multiplier_2 (.a(A), .b(B), .cout(multiplier_2_cout));  // open: out, cin
  mulh mulh_1 (.in_1(A), .in_2(B), .out_3(mulh_1_out_3));
  Divider #(.width(32)) divider_2 (.a(A), .b(B), .out(divider_2_out));  // open: upper, rem
  BitAdder #(.width(32)) bitadder_1 (.in0(A), .in1(B), .out(bitadder_1_out));
  assign bit_extender_2_out = {{25{1'b0}}, bitadder_1_out};  // Bit_Extender bit_extender_2
  Multiplexer #(.select(4), .width(32), .enable("false")) multiplexer_1 (
    .in0(and_1_out), .in1(or_1_out), .in2(xor_1_out), .in3(adder_1_out), .in4(subtractor_1_out),
    .in5(multiplier_1_out), .in6(multiplier_2_cout), .in7(mulh_1_out_3), .in8(divider_2_out), .in9(remu),
    .in10(srl0), .in11(sra0), .in12(sll0), .in13(slt0), .in14(bit_extender_2_out), .in15(B), .out(Result),
    .sel(ALUSel));

  // Notes on the sheet:
  //   INPUTS to your circuit
  //   mulhu
  //   DON'T CHANGE THE LOCATIONS OF THE INPUTS AND OUTPUTS!
  //   OUTPUT from your circuit
endmodule

module mulh (
  input  [31:0] in_1,
  input  [31:0] in_2,
  output [31:0] out_3
);

  wire xor_1_out;
  wire [31:0] multiplexer_1_out, multiplexer_2_out, multiplier_1_cout, negator_1_out, negator_2_out,
       negator_3_out, subtractor_1_out;

  Negator #(.width(32)) negator_1 (.in(in_1), .out(negator_1_out));
  Negator #(.width(32)) negator_2 (.in(in_2), .out(negator_2_out));
  Multiplexer #(.width(32), .enable("false")) multiplexer_1 (
    .in0(in_1), .in1(negator_1_out), .out(multiplexer_1_out), .sel(in_1[31]));
  Multiplexer #(.width(32), .enable("false")) multiplexer_2 (
    .in0(in_2), .in1(negator_2_out), .out(multiplexer_2_out), .sel(in_2[31]));
  Multiplier #(.width(32)) multiplier_1 (
    .a(multiplexer_1_out), .b(multiplexer_2_out), .cout(multiplier_1_cout));  // open: out, cin
  xor xor_1 (xor_1_out, in_1[31], in_2[31]);
  Negator #(.width(32)) negator_3 (.in(multiplier_1_cout), .out(negator_3_out));
  Subtractor #(.width(32)) subtractor_1 (.a(negator_3_out), .b(32'h1), .out(subtractor_1_out));  // open: bin, bout
  Multiplexer #(.width(32), .enable("false")) multiplexer_3 (
    .in0(multiplier_1_cout), .in1(subtractor_1_out), .out(out_3), .sel(xor_1_out));
endmodule

module sir (
  input  [31:0] in_1,
  input  [31:0] in_2,
  output [31:0] out_3
);

  Comparator #(.width(32), .mode("unsigned")) comparator_1 (
    .a(in_1),
    .b({in_2[0], in_2[1], in_2[2], in_2[3], in_2[4], in_2[5], in_2[6], in_2[7], in_2[8], in_2[9], in_2[10], in_2[11], in_2[12], in_2[13], in_2[14], in_2[15], in_2[16], in_2[17], in_2[18], in_2[19], in_2[20], in_2[21], in_2[22], in_2[23], in_2[24], in_2[25], in_2[26], in_2[27], in_2[28], in_2[29], in_2[30], in_2[31]}),
    .eq(out_3[0]));  // open: gt, lt

  assign out_3[31:1] = {31{1'b0}};
endmodule
