// Logisim project cpu.circ as structural Verilog: 4 circuits, main circuit main
module main (
  input  [31:0] INSTRUCTION,
  input  in_2,
  output [31:0] FETCH_ADDRESS,
  output [31:0] ra,
  output [31:0] sp,
  output [31:0] t0,
  output [31:0] t1,
  output [31:0] t2,
  output [31:0] s0,
  output [31:0] s1,
  output [31:0] a0
);

  wire Asel, BrEq, BrLT, BrUn, Bsel, MemRW, not_1_out, PCSel, RegWEn;
  wire [1:0] WBSel;
  wire [2:0] ImmSel;
  wire [3:0] ALUSel;
  wire [31:0] adder_1_out, ALU, divider_1_out, imm_gen_1_imm, inst1, main_1_read_data_1, main_1_read_data_2,
       main_2_readdata, multiplexer_1_out, multiplexer_2_out, multiplexer_3_out, multiplexer_4_out,
       multiplexer_5_out, PC, PC_plus_4, register_1_q;

  not not_1 (not_1_out, PCSel);
  Divider #(.width(32)) divider_1 (.a(ALU), .b(32'h4), .out(divider_1_out));  // open: upper, rem
  Multiplexer #(.width(32), .enable("false")) multiplexer_1 (
    .in0(adder_1_out), .in1(divider_1_out), .out(multiplexer_1_out), .sel(PCSel));
  Register #(.width(32)) u_PC (.D(multiplexer_1_out), .clk(in_2), .Q(FETCH_ADDRESS));  // open: en, clr
  Adder #(.width(32)) adder_1 (.a(32'h1), .b(FETCH_ADDRESS), .out(adder_1_out));  // open: cin, cout
  Multiplexer #(.width(32), .enable("false")) multiplexer_2 (
    .in0(32'h13), .in1(INSTRUCTION), .out(multiplexer_2_out), .sel(not_1_out));
  Register #(.width(32)) register_1 (.D(FETCH_ADDRESS), .clk(in_2), .Q(register_1_q));  // open: en, clr
  Imm_Gen imm_gen_1 (.inst(inst1), .ImmSel(ImmSel), .imm(imm_gen_1_imm));
  Register #(.width(32)) register_2 (.D(multiplexer_2_out), .clk(in_2), .Q(inst1));  // open: en, clr
  Clock clock_1 ();  // open: out
  Multiplier #(.width(32)) multiplier_1 (.a(register_1_q), .b(32'h4), .out(PC));  // open: cin, cout
  regfile_main main_1 (
    .rs2(inst1[24:20]), .rd(inst1[11:7]), .Read_Data_1(main_1_read_data_1), .Read_Data_2(main_1_read_data_2),
    .ra(ra), .sp(sp), .t0(t0), .t1(t1), .t2(t2), .s0(s0), .s1(s1), .a0(a0), .rs1(inst1[19:15]),
    .Write_Data(multiplexer_5_out), .RegWEn(RegWEn), .clk(in_2));
  Controller controller_1 (
    .Inst(inst1), .BrEq(BrEq), .BrLT(BrLT), .PCSel(PCSel), .ImmSel(ImmSel), .RegWEn(RegWEn), .BrUn(BrUn),
    .Asel(Asel), .Bsel(Bsel), .ALUSel(ALUSel), .MemRW(MemRW), .WBSel(WBSel));
  Adder #(.width(32)) adder_2 (.a(32'h4), .b(PC), .out(PC_plus_4));  // open: cin, cout
  Branch_Comp branch_comp_1 (.A(main_1_read_data_1), .B(main_1_read_data_2), .BrUn(BrUn), .BrLT(BrLT), .BrEq(BrEq));
  Multiplexer #(.width(32), .enable("false")) multiplexer_3 (
    .in0(main_1_read_data_1), .in1(PC), .out(multiplexer_3_out), .sel(Asel));
  Multiplexer #(.width(32), .enable("false")) multiplexer_4 (
    .in0(main_1_read_data_2), .in1(imm_gen_1_imm), .out(multiplexer_4_out), .sel(Bsel));
  alu Arithmetic_Logic_Unit (.A(multiplexer_3_out), .B(multiplexer_4_out), .ALUSel(ALUSel), .Result(ALU));
  mem_main main_2 (
    .WriteAddr(ALU), .MemRW(MemRW), .ReadData(main_2_readdata), .WriteData(main_1_read_data_2), .clk(in_2));
  Multiplexer #(.select(2), .width(32), .enable("false")) multiplexer_5 (
    .in0(main_2_readdata), .in1(ALU), .in2(PC_plus_4), .out(multiplexer_5_out), .sel(WBSel));  // open: in3

  // Other names for the same wires on the sheet: clk = in_2; fetch_addr[31:0] = FETCH_ADDRESS

  // Notes on the sheet:
  //   Output
  //   Inputs/Outputs from run.circ. DO NOT MOVE THESE.
  //   Inputs
  //   Inputs/Outputs from run.circ. DO NOT MOVE THESE.
endmodule

module Branch_Comp (
  input  [31:0] A,
  input  [31:0] B,
  input  BrUn,
  output BrLT,
  output BrEq
);

  wire [31:0] demultiplexer_1_out0, demultiplexer_1_out1, demultiplexer_2_out0, demultiplexer_2_out1,
       or_1_out, or_2_out;

  Demultiplexer #(.width(32), .enable("false")) demultiplexer_1 (
    .out0(demultiplexer_1_out0), .out1(demultiplexer_1_out1), .in(A), .sel(BrUn));
  Demultiplexer #(.width(32), .enable("false")) demultiplexer_2 (
    .out0(demultiplexer_2_out0), .out1(demultiplexer_2_out1), .in(B), .sel(BrUn));
  assign or_1_out = demultiplexer_1_out0 | demultiplexer_1_out1;  // OR_Gate or_1, 32 bits wide
  assign or_2_out = demultiplexer_2_out0 | demultiplexer_2_out1;  // OR_Gate or_2, 32 bits wide
  Comparator #(.width(32), .mode("unsigned")) comparator_1 (
    .a(or_1_out), .b(or_2_out), .eq(BrEq), .lt(BrLT));  // open: gt
endmodule

module Imm_Gen (
  input  [31:0] inst,
  input  [2:0] ImmSel,
  output [31:0] imm
);

  wire [31:0] btype, itype, jtype, stype;

  assign itype = {{20{inst[31]}}, inst[31:20]};  // Bit_Extender bit_extender_1
  assign stype = {{20{inst[31]}}, {inst[31:25], inst[11:7]}};  // Bit_Extender bit_extender_2
  assign btype = {{19{inst[31]}}, {inst[31], inst[7], inst[30:25], inst[11:8], 1'b0}};  // Bit_Extender bit_extender_3
  assign jtype = {{11{inst[31]}}, {inst[31], inst[19:12], inst[20], inst[30:21], 1'b0}};  // Bit_Extender bit_extender_4
  Multiplexer #(.select(3), .width(32), .enable("false")) multiplexer_1 (
    .in0(itype), .in1(stype), .in2(btype), .in3({inst[31:12], {12{1'b0}}}), .in4(jtype), .out(imm),
    .sel(ImmSel));  // open: in5, in6, in7

  // Other names for the same wires on the sheet: instruction[31:0] = inst; utype[31:12] = inst[31:12]
endmodule

module Controller (
  input  [31:0] Inst,
  input  BrEq,
  input  BrLT,
  output PCSel,
  output [2:0] ImmSel,
  output RegWEn,
  output BrUn,
  output Asel,
  output Bsel,
  output [3:0] ALUSel,
  output MemRW,
  output [1:0] WBSel
);

  wire and_1_out, and_2_out, and_3_out, and_4_out, and_5_out, and_6_out, and_7_out, and_8_out, and_9_out,
       and_10_out, and_11_out, and_12_out, and_13_out, and_14_out, and_15_out, and_16_out, and_17_out,
       and_18_out, and_19_out, and_20_out, and_21_out, and_22_out, and_23_out, and_24_out, and_25_out,
       and_26_out, and_27_out, and_28_out, and_29_out, and_30_out, and_31_out, and_32_out, and_33_out,
       and_34_out, and_35_out, comparator_1_eq, comparator_2_eq, comparator_3_eq, comparator_4_eq,
       comparator_5_eq, comparator_6_eq, comparator_7_eq, comparator_8_eq, comparator_9_eq, comparator_10_eq,
       comparator_11_eq, comparator_12_eq, comparator_13_eq, comparator_14_eq, comparator_15_eq,
       comparator_16_eq, comparator_17_eq, comparator_18_eq, comparator_19_eq, comparator_20_eq,
       comparator_21_eq, comparator_22_eq, comparator_23_eq, comparator_24_eq, comparator_25_eq,
       comparator_26_eq, comparator_27_eq, comparator_28_eq, comparator_29_eq, comparator_30_eq,
       comparator_31_eq, comparator_32_eq, comparator_33_eq, comparator_34_eq, comparator_35_eq,
       comparator_36_eq, comparator_37_eq, comparator_38_eq, comparator_39_eq, comparator_40_eq,
       comparator_41_eq, comparator_42_eq, comparator_43_eq, comparator_44_eq, comparator_45_eq,
       comparator_46_eq, comparator_47_eq, comparator_48_eq, comparator_49_eq, comparator_50_eq,
       comparator_51_eq, comparator_52_eq, comparator_53_eq, comparator_54_eq, comparator_55_eq,
       comparator_56_eq, comparator_57_eq, comparator_58_eq, comparator_59_eq, comparator_60_eq,
       comparator_61_eq, comparator_62_eq, comparator_63_eq, comparator_64_eq, comparator_65_eq,
       comparator_66_eq, comparator_67_eq, comparator_68_eq, comparator_69_eq, comparator_70_eq,
       comparator_71_eq, comparator_72_eq, comparator_73_eq, comparator_74_eq, comparator_75_eq,
       comparator_76_eq, comparator_77_eq, comparator_78_eq, comparator_79_eq, comparator_80_eq,
       comparator_81_eq, comparator_82_eq, comparator_83_eq, comparator_84_eq, comparator_85_eq,
       comparator_86_eq, comparator_87_eq, comparator_88_eq, comparator_89_eq, comparator_90_eq,
       comparator_91_eq, comparator_92_eq, comparator_93_eq, comparator_94_eq, comparator_95_eq,
       comparator_96_eq, comparator_97_eq;
  wire [6:0] addi, andi, auipc, beq1, beq2, bgeu, blt, bltu, bne1, bne2, jal, jalr, lb, lbu, lh, lhu, lui,
       lw, multiplexer_1_out, multiplexer_2_out, multiplexer_3_out, multiplexer_4_out, multiplexer_5_out,
       multiplexer_6_out, multiplexer_7_out, multiplexer_8_out, multiplexer_9_out, multiplexer_10_out,
       multiplexer_11_out, multiplexer_12_out, multiplexer_13_out, multiplexer_14_out, or_1_out, or_2_out,
       or_3_out, ori, slli, slti, srai, srli, sw, xori;

  Comparator #(.width(7)) comparator_1 (.a(Inst[6:0]), .b(7'b0110011), .eq(comparator_1_eq));  // open: gt, lt
  Comparator #(.width(3)) comparator_2 (.a(Inst[14:12]), .b(3'b000), .eq(comparator_2_eq));  // open: gt, lt
  Comparator #(.width(7)) comparator_3 (.a(Inst[31:25]), .b({7{1'b0}}), .eq(comparator_3_eq));  // open: gt, lt
  Comparator #(.width(7)) comparator_4 (.a(Inst[6:0]), .b(7'b0110011), .eq(comparator_4_eq));  // open: gt, lt
  Comparator #(.width(3)) comparator_5 (.a(Inst[14:12]), .b(3'b000), .eq(comparator_5_eq));  // open: gt, lt
  Comparator #(.width(7)) comparator_6 (.a(Inst[31:25]), .b(7'b0000001), .eq(comparator_6_eq));  // open: gt, lt
  Comparator #(.width(7)) comparator_7 (.a(Inst[6:0]), .b(7'b0110011), .eq(comparator_7_eq));  // open: gt, lt
  Comparator #(.width(3)) comparator_8 (.a(Inst[14:12]), .b(3'b000), .eq(comparator_8_eq));  // open: gt, lt
  Comparator #(.width(7)) comparator_9 (.a(Inst[31:25]), .b(7'b0100000), .eq(comparator_9_eq));  // open: gt, lt
  Comparator #(.width(7)) comparator_10 (.a(Inst[6:0]), .b(7'b0110011), .eq(comparator_10_eq));  // open: gt, lt
  Comparator #(.width(3)) comparator_11 (.a(Inst[14:12]), .b(3'b001), .eq(comparator_11_eq));  // open: gt, lt
  Comparator #(.width(7)) comparator_12 (.a(Inst[31:25]), .b({7{1'b0}}), .eq(comparator_12_eq));  // open: gt, lt
  Comparator #(.width(7)) comparator_13 (.a(Inst[6:0]), .b(7'b0110011), .eq(comparator_13_eq));  // open: gt, lt
  Comparator #(.width(3)) comparator_14 (.a(Inst[14:12]), .b(3'b001), .eq(comparator_14_eq));  // open: gt, lt
  Comparator #(.width(7)) comparator_15 (.a(Inst[31:25]), .b(7'b0000001), .eq(comparator_15_eq));  // open: gt, lt
  Comparator #(.width(7)) comparator_16 (.a(Inst[6:0]), .b(7'b0110011), .eq(comparator_16_eq));  // open: gt, lt
  Comparator #(.width(3)) comparator_17 (.a(Inst[14:12]), .b(3'b011), .eq(comparator_17_eq));  // open: gt, lt
  Comparator #(.width(7)) comparator_18 (.a(Inst[31:25]), .b(7'b0000001), .eq(comparator_18_eq));  // open: gt, lt
  Comparator #(.width(7)) comparator_19 (.a(Inst[6:0]), .b(7'b0110011), .eq(comparator_19_eq));  // open: gt, lt
  Comparator #(.width(3)) comparator_20 (.a(Inst[14:12]), .b(3'b010), .eq(comparator_20_eq));  // open: gt, lt
  Comparator #(.width(7)) comparator_21 (.a(Inst[31:25]), .b({7{1'b0}}), .eq(comparator_21_eq));  // open: gt, lt
  Comparator #(.width(7)) comparator_22 (.a(Inst[6:0]), .b(7'b0110011), .eq(comparator_22_eq));  // open: gt, lt
  Comparator #(.width(3)) comparator_23 (.a(Inst[14:12]), .b(3'b100), .eq(comparator_23_eq));  // open: gt, lt
  Comparator #(.width(7)) comparator_24 (.a(Inst[31:25]), .b({7{1'b0}}), .eq(comparator_24_eq));  // open: gt, lt
  Comparator #(.width(7)) comparator_25 (.a(Inst[6:0]), .b(7'b0110011), .eq(comparator_25_eq));  // open: gt, lt
  Comparator #(.width(3)) comparator_26 (.a(Inst[14:12]), .b(3'b101), .eq(comparator_26_eq));  // open: gt, lt
  Comparator #(.width(7)) comparator_27 (.a(Inst[31:25]), .b(7'b0000001), .eq(comparator_27_eq));  // open: gt, lt
  Comparator #(.width(7)) comparator_28 (.a(Inst[6:0]), .b(7'b0110011), .eq(comparator_28_eq));  // open: gt, lt
  Comparator #(.width(3)) comparator_29 (.a(Inst[14:12]), .b(3'b101), .eq(comparator_29_eq));  // open: gt, lt
  Comparator #(.width(7)) comparator_30 (.a(Inst[31:25]), .b({7{1'b0}}), .eq(comparator_30_eq));  // open: gt, lt
  Comparator #(.width(7)) comparator_31 (.a(Inst[6:0]), .b(7'b0110011), .eq(comparator_31_eq));  // open: gt, lt
  Comparator #(.width(3)) comparator_32 (.a(Inst[14:12]), .b(3'b110), .eq(comparator_32_eq));  // open: gt, lt
  Comparator #(.width(7)) comparator_33 (.a(Inst[31:25]), .b({7{1'b0}}), .eq(comparator_33_eq));  // open: gt, lt
  Comparator #(.width(7)) comparator_34 (.a(Inst[6:0]), .b(7'b0110011), .eq(comparator_34_eq));  // open: gt, lt
  Comparator #(.width(3)) comparator_35 (.a(Inst[14:12]), .b(3'b111), .eq(comparator_35_eq));  // open: gt, lt
  Comparator #(.width(7)) comparator_36 (.a(Inst[31:25]), .b(7'b0000001), .eq(comparator_36_eq));  // open: gt, lt
  Comparator #(.width(7)) comparator_37 (.a(Inst[6:0]), .b(7'b0110011), .eq(comparator_37_eq));  // open: gt, lt
  Comparator #(.width(3)) comparator_38 (.a(Inst[14:12]), .b(3'b111), .eq(comparator_38_eq));  // open: gt, lt
  Comparator #(.width(7)) comparator_39 (.a(Inst[31:25]), .b({7{1'b0}}), .eq(comparator_39_eq));  // open: gt, lt
  // Probe on Inst[6:0]
  // Probe on Inst[31:25]
  and and_1 (and_1_out, comparator_1_eq, comparator_2_eq, comparator_3_eq);
  and and_2 (and_2_out, comparator_4_eq, comparator_5_eq, comparator_6_eq);
  and and_3 (and_3_out, comparator_7_eq, comparator_8_eq, comparator_9_eq);
  and and_4 (and_4_out, comparator_10_eq, comparator_11_eq, comparator_12_eq);
  and and_5 (and_5_out, comparator_13_eq, comparator_14_eq, comparator_15_eq);
  and and_6 (and_6_out, comparator_16_eq, comparator_17_eq, comparator_18_eq);
  and and_7 (and_7_out, comparator_19_eq, comparator_20_eq, comparator_21_eq);
  and and_8 (and_8_out, comparator_22_eq, comparator_23_eq, comparator_24_eq);
  and and_9 (and_9_out, comparator_25_eq, comparator_26_eq, comparator_27_eq);
  and and_10 (and_10_out, comparator_28_eq, comparator_29_eq, comparator_30_eq);
  and and_11 (and_11_out, comparator_31_eq, comparator_32_eq, comparator_33_eq);
  and and_12 (and_12_out, comparator_34_eq, comparator_35_eq, comparator_36_eq);
  and and_13 (and_13_out, comparator_37_eq, comparator_38_eq, comparator_39_eq);
  Comparator #(.width(32), .mode("unsigned")) comparator_40 (
    .a(Inst), .b({32{1'b0}}), .eq(comparator_40_eq));  // open: gt, lt
  Multiplexer #(.width(7), .enable("false")) multiplexer_1 (
    .in0({7{1'b0}}), .in1({7{1'b0}}), .out(multiplexer_1_out), .sel(and_1_out));
  Multiplexer #(.width(7), .enable("false")) multiplexer_2 (
    .in0({7{1'b0}}), .in1(7'b0000001), .out(multiplexer_2_out), .sel(and_2_out));
  Multiplexer #(.width(7), .enable("false")) multiplexer_3 (
    .in0({7{1'b0}}), .in1(7'b0000010), .out(multiplexer_3_out), .sel(and_3_out));
  Multiplexer #(.width(7), .enable("false")) multiplexer_4 (
    .in0({7{1'b0}}), .in1(7'b0000011), .out(multiplexer_4_out), .sel(and_4_out));
  Multiplexer #(.width(7), .enable("false")) multiplexer_5 (
    .in0({7{1'b0}}), .in1(7'b0000100), .out(multiplexer_5_out), .sel(and_5_out));
  Multiplexer #(.width(7), .enable("false")) multiplexer_6 (
    .in0({7{1'b0}}), .in1(7'b0000101), .out(multiplexer_6_out), .sel(and_6_out));
  Multiplexer #(.width(7), .enable("false")) multiplexer_7 (
    .in0({7{1'b0}}), .in1(7'b0000110), .out(multiplexer_7_out), .sel(and_7_out));
  Multiplexer #(.width(7), .enable("false")) multiplexer_8 (
    .in0({7{1'b0}}), .in1(7'b0000111), .out(multiplexer_8_out), .sel(and_8_out));
  Multiplexer #(.width(7), .enable("false")) multiplexer_9 (
    .in0({7{1'b0}}), .in1(7'b0001000), .out(multiplexer_9_out), .sel(and_9_out));
  Multiplexer #(.width(7), .enable("false")) multiplexer_10 (
    .in0({7{1'b0}}), .in1(7'b0001001), .out(multiplexer_10_out), .sel(and_10_out));
  Multiplexer #(.width(7), .enable("false")) multiplexer_11 (
    .in0({7{1'b0}}), .in1(7'b0001010), .out(multiplexer_11_out), .sel(and_11_out));
  Multiplexer #(.width(7), .enable("false")) multiplexer_12 (
    .in0({7{1'b0}}), .in1(7'b0001011), .out(multiplexer_12_out), .sel(and_12_out));
  Multiplexer #(.width(7), .enable("false")) multiplexer_13 (
    .in0({7{1'b0}}), .in1(7'b0001100), .out(multiplexer_13_out), .sel(and_13_out));
  // Probe on Inst[14:12]
  Multiplexer #(.width(7), .enable("false")) multiplexer_14 (
    .in0({7{1'b0}}), .in1(7'b0100110), .out(multiplexer_14_out), .sel(comparator_40_eq));
  assign or_1_out = multiplexer_1_out | multiplexer_2_out | multiplexer_3_out | multiplexer_4_out | multiplexer_5_out | multiplexer_6_out | multiplexer_7_out | multiplexer_8_out | multiplexer_9_out | multiplexer_10_out | multiplexer_11_out | multiplexer_12_out | multiplexer_13_out | lb | lh | lw | lbu | lhu | addi | slli | slti | xori | srli | srai | ori | andi | sw | beq1 | beq2 | blt | bltu | bne1;  // OR_Gate or_1, 7 bits wide
  assign or_2_out = bne2 | bgeu | auipc | lui | jal | jalr;  // OR_Gate or_2, 7 bits wide
  // Probe on or_3_out
  assign or_3_out = or_1_out | multiplexer_14_out | or_2_out;  // OR_Gate or_3, 7 bits wide
  ROM #(.addrWidth(7), .dataWidth(15)) rom_1 (
    .addr(or_3_out), .data({PCSel, ImmSel, RegWEn, BrUn, Asel, Bsel, ALUSel, MemRW, WBSel}));
  Comparator #(.width(7)) comparator_41 (.a(Inst[6:0]), .b(7'b0000011), .eq(comparator_41_eq));  // open: gt, lt
  Comparator #(.width(3)) comparator_42 (.a(Inst[14:12]), .b(3'b000), .eq(comparator_42_eq));  // open: gt, lt
  Comparator #(.width(7)) comparator_43 (.a(Inst[6:0]), .b(7'b0000011), .eq(comparator_43_eq));  // open: gt, lt
  Comparator #(.width(3)) comparator_44 (.a(Inst[14:12]), .b(3'b001), .eq(comparator_44_eq));  // open: gt, lt
  Comparator #(.width(7)) comparator_45 (.a(Inst[6:0]), .b(7'b0000011), .eq(comparator_45_eq));  // open: gt, lt
  Comparator #(.width(3)) comparator_46 (.a(Inst[14:12]), .b(3'b010), .eq(comparator_46_eq));  // open: gt, lt
  Comparator #(.width(7)) comparator_47 (.a(Inst[6:0]), .b(7'b0000011), .eq(comparator_47_eq));  // open: gt, lt
  Comparator #(.width(3)) comparator_48 (.a(Inst[14:12]), .b(3'b100), .eq(comparator_48_eq));  // open: gt, lt
  Comparator #(.width(7)) comparator_49 (.a(Inst[6:0]), .b(7'b0000011), .eq(comparator_49_eq));  // open: gt, lt
  Comparator #(.width(3)) comparator_50 (.a(Inst[14:12]), .b(3'b101), .eq(comparator_50_eq));  // open: gt, lt
  Comparator #(.width(7)) comparator_51 (.a(Inst[6:0]), .b(7'b0010011), .eq(comparator_51_eq));  // open: gt, lt
  Comparator #(.width(3)) comparator_52 (.a(Inst[14:12]), .b(3'b000), .eq(comparator_52_eq));  // open: gt, lt
  Comparator #(.width(7)) comparator_53 (.a(Inst[6:0]), .b(7'b0010011), .eq(comparator_53_eq));  // open: gt, lt
  Comparator #(.width(3)) comparator_54 (.a(Inst[14:12]), .b(3'b001), .eq(comparator_54_eq));  // open: gt, lt
  Comparator #(.width(7)) comparator_55 (.a(Inst[31:25]), .b({7{1'b0}}), .eq(comparator_55_eq));  // open: gt, lt
  Comparator #(.width(7)) comparator_56 (.a(Inst[6:0]), .b(7'b0010011), .eq(comparator_56_eq));  // open: gt, lt
  Comparator #(.width(3)) comparator_57 (.a(Inst[14:12]), .b(3'b010), .eq(comparator_57_eq));  // open: gt, lt
  Comparator #(.width(7)) comparator_58 (.a(Inst[6:0]), .b(7'b0010011), .eq(comparator_58_eq));  // open: gt, lt
  Comparator #(.width(3)) comparator_59 (.a(Inst[14:12]), .b(3'b100), .eq(comparator_59_eq));  // open: gt, lt
  Comparator #(.width(7)) comparator_60 (.a(Inst[6:0]), .b(7'b0010011), .eq(comparator_60_eq));  // open: gt, lt
  Comparator #(.width(3)) comparator_61 (.a(Inst[14:12]), .b(3'b101), .eq(comparator_61_eq));  // open: gt, lt
  Comparator #(.width(7)) comparator_62 (.a(Inst[31:25]), .b({7{1'b0}}), .eq(comparator_62_eq));  // open: gt, lt
  Comparator #(.width(7)) comparator_63 (.a(Inst[6:0]), .b(7'b0010011), .eq(comparator_63_eq));  // open: gt, lt
  Comparator #(.width(3)) comparator_64 (.a(Inst[14:12]), .b(3'b101), .eq(comparator_64_eq));  // open: gt, lt
  Comparator #(.width(7)) comparator_65 (.a(Inst[31:25]), .b(7'b0100000), .eq(comparator_65_eq));  // open: gt, lt
  Comparator #(.width(7)) comparator_66 (.a(Inst[6:0]), .b(7'b0010011), .eq(comparator_66_eq));  // open: gt, lt
  Comparator #(.width(3)) comparator_67 (.a(Inst[14:12]), .b(3'b110), .eq(comparator_67_eq));  // open: gt, lt
  Comparator #(.width(7)) comparator_68 (.a(Inst[6:0]), .b(7'b0010011), .eq(comparator_68_eq));  // open: gt, lt
  Comparator #(.width(3)) comparator_69 (.a(Inst[14:12]), .b(3'b111), .eq(comparator_69_eq));  // open: gt, lt
  Multiplexer #(.width(7), .enable("false")) multiplexer_15 (
    .in0({7{1'b0}}), .in1(7'b0001101), .out(lb), .sel(and_14_out));
  and and_14 (and_14_out, comparator_41_eq, comparator_42_eq);
  Multiplexer #(.width(7), .enable("false")) multiplexer_16 (
    .in0({7{1'b0}}), .in1(7'b0001110), .out(lh), .sel(and_15_out));
  and and_15 (and_15_out, comparator_43_eq, comparator_44_eq);
  Multiplexer #(.width(7), .enable("false")) multiplexer_17 (
    .in0({7{1'b0}}), .in1(7'b0001111), .out(lw), .sel(and_16_out));
  and and_16 (and_16_out, comparator_45_eq, comparator_46_eq);
  Multiplexer #(.width(7), .enable("false")) multiplexer_18 (
    .in0({7{1'b0}}), .in1(7'b0010000), .out(lbu), .sel(and_17_out));
  and and_17 (and_17_out, comparator_47_eq, comparator_48_eq);
  Multiplexer #(.width(7), .enable("false")) multiplexer_19 (
    .in0({7{1'b0}}), .in1(7'b0010001), .out(lhu), .sel(and_18_out));
  and and_18 (and_18_out, comparator_49_eq, comparator_50_eq);
  Multiplexer #(.width(7), .enable("false")) multiplexer_20 (
    .in0({7{1'b0}}), .in1(7'b0010010), .out(addi), .sel(and_19_out));
  and and_19 (and_19_out, comparator_51_eq, comparator_52_eq);
  Multiplexer #(.width(7), .enable("false")) multiplexer_21 (
    .in0({7{1'b0}}), .in1(7'b0010011), .out(slli), .sel(and_20_out));
  and and_20 (and_20_out, comparator_53_eq, comparator_54_eq, comparator_55_eq);
  Multiplexer #(.width(7), .enable("false")) multiplexer_22 (
    .in0({7{1'b0}}), .in1(7'b0010100), .out(slti), .sel(and_21_out));
  and and_21 (and_21_out, comparator_56_eq, comparator_57_eq);
  Multiplexer #(.width(7), .enable("false")) multiplexer_23 (
    .in0({7{1'b0}}), .in1(7'b0010101), .out(xori), .sel(and_22_out));
  and and_22 (and_22_out, comparator_58_eq, comparator_59_eq);
  Multiplexer #(.width(7), .enable("false")) multiplexer_24 (
    .in0({7{1'b0}}), .in1(7'b0010110), .out(srli), .sel(and_23_out));
  and and_23 (and_23_out, comparator_60_eq, comparator_61_eq, comparator_62_eq);
  Multiplexer #(.width(7), .enable("false")) multiplexer_25 (
    .in0({7{1'b0}}), .in1(7'b0010111), .out(srai), .sel(and_24_out));
  and and_24 (and_24_out, comparator_63_eq, comparator_64_eq, comparator_65_eq);
  Multiplexer #(.width(7), .enable("false")) multiplexer_26 (
    .in0({7{1'b0}}), .in1(7'b0011000), .out(ori), .sel(and_25_out));
  and and_25 (and_25_out, comparator_66_eq, comparator_67_eq);
  Multiplexer #(.width(7), .enable("false")) multiplexer_27 (
    .in0({7{1'b0}}), .in1(7'b0011001), .out(andi), .sel(and_26_out));
  and and_26 (and_26_out, comparator_68_eq, comparator_69_eq);
  Comparator #(.width(7)) comparator_70 (.a(Inst[6:0]), .b(7'b0100011), .eq(comparator_70_eq));  // open: gt, lt
  Comparator #(.width(3)) comparator_71 (.a(Inst[14:12]), .b(3'b010), .eq(comparator_71_eq));  // open: gt, lt
  Comparator #(.width(7)) comparator_72 (.a(Inst[6:0]), .b(7'b1100011), .eq(comparator_72_eq));  // open: gt, lt
  Comparator #(.width(3)) comparator_73 (.a(Inst[14:12]), .b(3'b000), .eq(comparator_73_eq));  // open: gt, lt
  Comparator #(.width(1)) comparator_74 (.a(BrEq), .b(1'b0), .eq(comparator_74_eq));  // open: gt, lt
  Comparator #(.width(7)) comparator_75 (.a(Inst[6:0]), .b(7'b1100011), .eq(comparator_75_eq));  // open: gt, lt
  Comparator #(.width(3)) comparator_76 (.a(Inst[14:12]), .b(3'b000), .eq(comparator_76_eq));  // open: gt, lt
  Comparator #(.width(1)) comparator_77 (.a(BrEq), .b(1'b1), .eq(comparator_77_eq));  // open: gt, lt
  Comparator #(.width(7)) comparator_78 (.a(Inst[6:0]), .b(7'b1100011), .eq(comparator_78_eq));  // open: gt, lt
  Comparator #(.width(3)) comparator_79 (.a(Inst[14:12]), .b(3'b001), .eq(comparator_79_eq));  // open: gt, lt
  Comparator #(.width(1)) comparator_80 (.a(BrEq), .b(1'b0), .eq(comparator_80_eq));  // open: gt, lt
  Comparator #(.width(7)) comparator_81 (.a(Inst[6:0]), .b(7'b1100011), .eq(comparator_81_eq));  // open: gt, lt
  Comparator #(.width(3)) comparator_82 (.a(Inst[14:12]), .b(3'b001), .eq(comparator_82_eq));  // open: gt, lt
  Comparator #(.width(1)) comparator_83 (.a(BrEq), .b(1'b1), .eq(comparator_83_eq));  // open: gt, lt
  Comparator #(.width(7)) comparator_84 (.a(Inst[6:0]), .b(7'b1100011), .eq(comparator_84_eq));  // open: gt, lt
  Comparator #(.width(3)) comparator_85 (.a(Inst[14:12]), .b(3'b111), .eq(comparator_85_eq));  // open: gt, lt
  Comparator #(.width(1)) comparator_86 (.a(BrLT), .b(1'b0), .eq(comparator_86_eq));  // open: gt, lt
  Comparator #(.width(7)) comparator_87 (.a(Inst[6:0]), .b(7'b0010111), .eq(comparator_87_eq));  // open: gt, lt
  Comparator #(.width(7)) comparator_88 (.a(Inst[6:0]), .b(7'b0110111), .eq(comparator_88_eq));  // open: gt, lt
  Comparator #(.width(7)) comparator_89 (.a(Inst[6:0]), .b(7'b1101111), .eq(comparator_89_eq));  // open: gt, lt
  Comparator #(.width(7)) comparator_90 (.a(Inst[6:0]), .b(7'b1100111), .eq(comparator_90_eq));  // open: gt, lt
  Comparator #(.width(3)) comparator_91 (.a(Inst[14:12]), .b(3'b000), .eq(comparator_91_eq));  // open: gt, lt
  Multiplexer #(.width(7), .enable("false")) multiplexer_28 (
    .in0({7{1'b0}}), .in1(7'b0011010), .out(sw), .sel(and_27_out));
  and and_27 (and_27_out, comparator_70_eq, comparator_71_eq);
  Multiplexer #(.width(7), .enable("false")) multiplexer_29 (
    .in0({7{1'b0}}), .in1(7'b0011011), .out(beq1), .sel(and_28_out));
  and and_28 (and_28_out, comparator_72_eq, comparator_73_eq, comparator_74_eq);
  Multiplexer #(.width(7), .enable("false")) multiplexer_30 (
    .in0({7{1'b0}}), .in1(7'b0011100), .out(beq2), .sel(and_29_out));
  and and_29 (and_29_out, comparator_75_eq, comparator_76_eq, comparator_77_eq);
  Multiplexer #(.width(7), .enable("false")) multiplexer_31 (
    .in0({7{1'b0}}), .in1(7'b0011111), .out(bne1), .sel(and_30_out));
  and and_30 (and_30_out, comparator_78_eq, comparator_79_eq, comparator_80_eq);
  Multiplexer #(.width(7), .enable("false")) multiplexer_32 (
    .in0({7{1'b0}}), .in1(7'b0100000), .out(bne2), .sel(and_31_out));
  and and_31 (and_31_out, comparator_81_eq, comparator_82_eq, comparator_83_eq);
  Multiplexer #(.width(7), .enable("false")) multiplexer_33 (
    .in0({7{1'b0}}), .in1(7'b0100001), .out(bgeu), .sel(and_32_out));
  and and_32 (and_32_out, comparator_84_eq, comparator_85_eq, comparator_86_eq);
  Multiplexer #(.width(7), .enable("false")) multiplexer_34 (
    .in0({7{1'b0}}), .in1(7'b0100010), .out(auipc), .sel(comparator_87_eq));
  Multiplexer #(.width(7), .enable("false")) multiplexer_35 (
    .in0({7{1'b0}}), .in1(7'b0100011), .out(lui), .sel(comparator_88_eq));
  Multiplexer #(.width(7), .enable("false")) multiplexer_36 (
    .in0({7{1'b0}}), .in1(7'b0100100), .out(jal), .sel(comparator_89_eq));
  Multiplexer #(.width(7), .enable("false")) multiplexer_37 (
    .in0({7{1'b0}}), .in1(7'b0100101), .out(jalr), .sel(and_33_out));
  and and_33 (and_33_out, comparator_90_eq, comparator_91_eq);
  Comparator #(.width(7)) comparator_92 (.a(Inst[6:0]), .b(7'b1100011), .eq(comparator_92_eq));  // open: gt, lt
  Comparator #(.width(3)) comparator_93 (.a(Inst[14:12]), .b(3'b100), .eq(comparator_93_eq));  // open: gt, lt
  Comparator #(.width(1)) comparator_94 (.a(BrLT), .b(1'b1), .eq(comparator_94_eq));  // open: gt, lt
  Comparator #(.width(7)) comparator_95 (.a(Inst[6:0]), .b(7'b1100011), .eq(comparator_95_eq));  // open: gt, lt
  Comparator #(.width(3)) comparator_96 (.a(Inst[14:12]), .b(3'b110), .eq(comparator_96_eq));  // open: gt, lt
  Comparator #(.width(1)) comparator_97 (.a(BrLT), .b(1'b1), .eq(comparator_97_eq));  // open: gt, lt
  Multiplexer #(.width(7), .enable("false")) multiplexer_38 (
    .in0({7{1'b0}}), .in1(7'b0011101), .out(blt), .sel(and_34_out));
  and and_34 (and_34_out, comparator_92_eq, comparator_93_eq, comparator_94_eq);
  Multiplexer #(.width(7), .enable("false")) multiplexer_39 (
    .in0({7{1'b0}}), .in1(7'b0011110), .out(bltu), .sel(and_35_out));
  and and_35 (and_35_out, comparator_95_eq, comparator_96_eq, comparator_97_eq);

  // Other names for the same wires on the sheet: opcode[6:0] = Inst[6:0]; funct3[2:0] = Inst[14:12];
  //   funct7[6:0] = Inst[31:25]

  // Notes on the sheet:
  //   R
  //   add
  //   mul
  //   mul
  //   sub
  //   sll
  //   mulh
  //   mulhu
  //   slt
  //   xor
  //   divu
  //   srl
  //   or
  //   reum
  //   and
  //   contents of rom_1 (hex, n*v repeats v):
  //   419 429 421 461 439 431 469 411 441 451 409 449 401 418 418 498 418 418 499 4e1 4e9 491 4d1 4d9 489
  //   481 89c 1198 5198 5198 5398 5198 1398 5398 1d99 1cf9 659a 449a
  //   I
  //   lb
  //   lh
  //   lw
  //   lbu
  //   lhu
  //   addi
  //   slli
  //   slti
  //   xori
  //   srli
  //   srai
  //   ori
  //   andi
  //   S
  //   SB
  //   sw
  //   beq
  //   beq
  //   bne
  //   bne
  //   bgeu
  //   auipc
  //   lui
  //   UJ
  //   jal
  //   I
  //   jalr
  //   U
  //   blt
  //   bltu
endmodule
