// Logisim project mem.circ as structural Verilog: 1 circuit, main circuit main
module main (
  input  [31:0] WriteAddr,
  input  MemRW,
  input  clk,
  input  [31:0] WriteData,
  output [31:0] ReadData
);

  RAM #(.addrWidth(14), .dataWidth(32), .trigger("falling"), .databus("bibus")) ram_1 (
    .addr(WriteAddr[13:0]), .we(MemRW), .oe(1'b1), .clk(clk), .din(WriteData), .dout(ReadData));
endmodule
